// Logisim project Memorii_fifo.circ as structural Verilog
module main (
  input  in_1,
  input  in_2,
  input  in_3,
  input  in_4,
  input  in_5,
  input  in_6,
  input  in_7,
  input  in_8,
  input  in_9,
  input  in_10,
  input  in_11
);

  wire clock_1_out, n7447_1_pin3, n7447_1_pin9, n7447_1_pin10, n7447_1_pin11, n7447_1_pin12, n7447_1_pin13,
       n7447_1_pin14, n7447_1_pin15, n7447_2_pin3, n7447_2_pin9, n7447_2_pin10, n7447_2_pin11, n7447_2_pin12,
       n7447_2_pin13, n7447_2_pin14, n7447_2_pin15, n7447_3_pin3, n7447_3_pin9, n7447_3_pin10, n7447_3_pin11,
       n7447_3_pin12, n7447_3_pin13, n7447_3_pin14, n7447_3_pin15, n7447_4_pin3, n7447_4_pin9, n7447_4_pin10,
       n7447_4_pin11, n7447_4_pin12, n7447_4_pin13, n7447_4_pin14, n7447_4_pin15, n7447_5_pin3, n7447_5_pin9,
       n7447_5_pin10, n7447_5_pin11, n7447_5_pin12, n7447_5_pin13, n7447_5_pin14, n7447_5_pin15,
       status_component_1_empty, status_component_1_full, unit_command_1_direction_count,
       unit_command_1_enable_count, unit_command_1_enable_pop, unit_command_1_enable_push,
       unit_command_1_enable_ram, unit_command_1_reset_empty_operation, unit_command_1_selection,
       unit_command_1_write;
  wire [3:0] converter_binary_to_decimal_1_decimal_digit, converter_binary_to_decimal_1_unit_digit,
       converter_binary_to_decimal_2_decimal_digit, converter_binary_to_decimal_2_hundred_digit,
       converter_binary_to_decimal_2_unit_digit;
  wire [4:0] multiplexor_2_1_5_bits_1_result, revese_direct_counter_1_count, revese_direct_counter_2_count,
       revese_direct_counter_3_count;
  wire [7:0] memory_ram_1_data_output;

  Clock clock_1 (.out(clock_1_out));
  unit_command unit_command_1 (
    .push(in_9), .pop(in_10), .clk(clock_1_out), .empty(status_component_1_empty), .empty_operation(in_11),
    .full(status_component_1_full), .reset_empty_operation(unit_command_1_reset_empty_operation),
    .enable_push(unit_command_1_enable_push), .enable_pop(unit_command_1_enable_pop),
    .enable_count(unit_command_1_enable_count), .direction_count(unit_command_1_direction_count),
    .write(unit_command_1_write), .selection(unit_command_1_selection), .enable_ram(unit_command_1_enable_ram));
  revese_direct_counter revese_direct_counter_1 (
    .enable(unit_command_1_enable_push), .direction(1'b1), .reset(unit_command_1_reset_empty_operation),
    .clk(clock_1_out), .count(revese_direct_counter_1_count));
  revese_direct_counter revese_direct_counter_2 (
    .enable(unit_command_1_enable_pop), .direction(1'b1), .reset(unit_command_1_reset_empty_operation),
    .clk(clock_1_out), .count(revese_direct_counter_2_count));
  revese_direct_counter revese_direct_counter_3 (
    .enable(unit_command_1_enable_count), .direction(unit_command_1_direction_count),
    .reset(unit_command_1_reset_empty_operation), .clk(clock_1_out), .count(revese_direct_counter_3_count));
  multiplexor_2_1_5_bits multiplexor_2_1_5_bits_1 (
    .a(revese_direct_counter_1_count), .b(revese_direct_counter_2_count), .sel(unit_command_1_selection),
    .result(multiplexor_2_1_5_bits_1_result));
  status_component status_component_1 (
    .number_elements(revese_direct_counter_3_count), .empty(status_component_1_empty),
    .full(status_component_1_full));
  converter_binary_to_decimal converter_binary_to_decimal_1 (
    .number_in_digit({3'b000, revese_direct_counter_3_count}),
    .unit_digit(converter_binary_to_decimal_1_unit_digit),
    .decimal_digit(converter_binary_to_decimal_1_decimal_digit));  // open: hundred_digit
  memory_ram memory_ram_1 (
    .address(multiplexor_2_1_5_bits_1_result), .enable(unit_command_1_enable_ram),
    .reset(unit_command_1_reset_empty_operation), .w_r(unit_command_1_write), .clk(clock_1_out),
    .data_input({in_8, in_7, in_6, in_5, in_4, in_3, in_2, in_1}), .data_output(memory_ram_1_data_output));
  LED led_1 (.in(status_component_1_empty));
  LED led_2 (.in(status_component_1_full));
  converter_binary_to_decimal converter_binary_to_decimal_2 (
    .number_in_digit(memory_ram_1_data_output), .unit_digit(converter_binary_to_decimal_2_unit_digit),
    .decimal_digit(converter_binary_to_decimal_2_decimal_digit),
    .hundred_digit(converter_binary_to_decimal_2_hundred_digit));
  _7447 u_7447_1 (
    .pin1(converter_binary_to_decimal_1_decimal_digit[1]),
    .pin2(converter_binary_to_decimal_1_decimal_digit[2]), .pin3(n7447_1_pin3), .pin4(n7447_1_pin3),
    .pin5(n7447_1_pin3), .pin6(converter_binary_to_decimal_1_decimal_digit[3]),
    .pin7(converter_binary_to_decimal_1_decimal_digit[0]), .pin15(n7447_1_pin15), .pin14(n7447_1_pin14),
    .pin13(n7447_1_pin13), .pin12(n7447_1_pin12), .pin11(n7447_1_pin11), .pin10(n7447_1_pin10),
    .pin9(n7447_1_pin9));
  _7447 u_7447_2 (
    .pin1(converter_binary_to_decimal_1_unit_digit[1]), .pin2(converter_binary_to_decimal_1_unit_digit[2]),
    .pin3(n7447_2_pin3), .pin4(n7447_2_pin3), .pin5(n7447_2_pin3),
    .pin6(converter_binary_to_decimal_1_unit_digit[3]), .pin7(converter_binary_to_decimal_1_unit_digit[0]),
    .pin15(n7447_2_pin15), .pin14(n7447_2_pin14), .pin13(n7447_2_pin13), .pin12(n7447_2_pin12),
    .pin11(n7447_2_pin11), .pin10(n7447_2_pin10), .pin9(n7447_2_pin9));
  _7_Segment_Display #(.active("false"), .decimalPoint("false")) u_7_segment_display_1 (
    .g(n7447_1_pin14), .f(n7447_1_pin15), .a(n7447_1_pin13), .b(n7447_1_pin12), .e(n7447_1_pin9),
    .d(n7447_1_pin10), .c(n7447_1_pin11));
  _7_Segment_Display #(.active("false"), .decimalPoint("false")) u_7_segment_display_2 (
    .g(n7447_2_pin14), .f(n7447_2_pin15), .a(n7447_2_pin13), .b(n7447_2_pin12), .e(n7447_2_pin9),
    .d(n7447_2_pin10), .c(n7447_2_pin11));
  _7447 u_7447_3 (
    .pin1(converter_binary_to_decimal_2_hundred_digit[1]),
    .pin2(converter_binary_to_decimal_2_hundred_digit[2]), .pin3(n7447_3_pin3), .pin4(n7447_3_pin3),
    .pin5(n7447_3_pin3), .pin6(converter_binary_to_decimal_2_hundred_digit[3]),
    .pin7(converter_binary_to_decimal_2_hundred_digit[0]), .pin15(n7447_3_pin15), .pin14(n7447_3_pin14),
    .pin13(n7447_3_pin13), .pin12(n7447_3_pin12), .pin11(n7447_3_pin11), .pin10(n7447_3_pin10),
    .pin9(n7447_3_pin9));
  _7447 u_7447_4 (
    .pin1(converter_binary_to_decimal_2_decimal_digit[1]),
    .pin2(converter_binary_to_decimal_2_decimal_digit[2]), .pin3(n7447_4_pin3), .pin4(n7447_4_pin3),
    .pin5(n7447_4_pin3), .pin6(converter_binary_to_decimal_2_decimal_digit[3]),
    .pin7(converter_binary_to_decimal_2_decimal_digit[0]), .pin15(n7447_4_pin15), .pin14(n7447_4_pin14),
    .pin13(n7447_4_pin13), .pin12(n7447_4_pin12), .pin11(n7447_4_pin11), .pin10(n7447_4_pin10),
    .pin9(n7447_4_pin9));
  _7447 u_7447_5 (
    .pin1(converter_binary_to_decimal_2_unit_digit[1]), .pin2(converter_binary_to_decimal_2_unit_digit[2]),
    .pin3(n7447_5_pin3), .pin4(n7447_5_pin3), .pin5(n7447_5_pin3),
    .pin6(converter_binary_to_decimal_2_unit_digit[3]), .pin7(converter_binary_to_decimal_2_unit_digit[0]),
    .pin15(n7447_5_pin15), .pin14(n7447_5_pin14), .pin13(n7447_5_pin13), .pin12(n7447_5_pin12),
    .pin11(n7447_5_pin11), .pin10(n7447_5_pin10), .pin9(n7447_5_pin9));
  _7_Segment_Display #(.active("false"), .decimalPoint("false")) u_7_segment_display_3 (
    .g(n7447_3_pin14), .f(n7447_3_pin15), .a(n7447_3_pin13), .b(n7447_3_pin12), .e(n7447_3_pin9),
    .d(n7447_3_pin10), .c(n7447_3_pin11));
  _7_Segment_Display #(.active("false"), .decimalPoint("false")) u_7_segment_display_4 (
    .g(n7447_4_pin14), .f(n7447_4_pin15), .a(n7447_4_pin13), .b(n7447_4_pin12), .e(n7447_4_pin9),
    .d(n7447_4_pin10), .c(n7447_4_pin11));
  _7_Segment_Display #(.active("false"), .decimalPoint("false")) u_7_segment_display_5 (
    .g(n7447_5_pin14), .f(n7447_5_pin15), .a(n7447_5_pin13), .b(n7447_5_pin12), .e(n7447_5_pin9),
    .d(n7447_5_pin10), .c(n7447_5_pin11));
  // also tied to VCC on the sheet: {n7447_1_pin3, n7447_2_pin3, n7447_3_pin3, n7447_4_pin3, n7447_5_pin3}

  // Notes on the sheet:
  //   Numarator Push - Up
  //   Numarator Pop - Up
  //   Numarator Elemnte Coada
  //   Empty
  //   Full
  //   Numar Elemente in Coada
  //   Sute
  //   Zeci
  //   Unitati
endmodule

// VHDL entity converter_binary_to_decimal, as the project stores it:
--------------------------------------------------------------------------------
-- Project : Memorii FIFO
-- Autor   : Cret Maria-Magdalena
--------------------------------------------------------------------------------
-- Description : Implementarea unui convertor din binar in zecimal
--------------------------------------------------------------------------------

LIBRARY ieee;
USE ieee.std_logic_1164.all;
USE ieee.std_logic_unsigned.all;
USE ieee.std_logic_arith.all;
USE ieee.numeric_std.all;

ENTITY converter_binary_to_decimal IS
  PORT (
  number_in_digit: in std_logic_vector(7 downto 0);
  unit_digit: out std_logic_vector(3 downto 0);
  decimal_digit: out std_logic_vector(3 downto 0); 
  hundred_digit: out std_logic_vector(3 downto 0)
    );
END converter_binary_to_decimal;


ARCHITECTURE TypeArchitecture OF converter_binary_to_decimal IS
signal number_decimal, unit_decimal, decimal_decimal, hundred_decimal : integer;
BEGIN
	number_decimal<= conv_integer(number_in_digit);
	unit_decimal<=number_decimal rem 10;
	decimal_decimal<=(number_decimal rem 100)/10;
	hundred_decimal<=number_decimal/100;

	process(unit_decimal, decimal_decimal, hundred_decimal)
	begin
		unit_digit<=std_logic_vector(to_unsigned(unit_decimal, 4));
		decimal_digit<=std_logic_vector(to_unsigned(decimal_decimal, 4));
		hundred_digit<=std_logic_vector(to_unsigned(hundred_decimal, 4));
	end process;

END TypeArchitecture;

// VHDL entity memory_ram, as the project stores it:
--------------------------------------------------------------------------------
-- Project : Memorii FIFO
-- Autor   : Cret Maria-Magdalena 
--------------------------------------------------------------------------------
-- Description : implementarea memoriei RAM
--------------------------------------------------------------------------------

LIBRARY ieee;
USE ieee.std_logic_1164.all;
USE ieee.numeric_std.all;

ENTITY memory_ram IS
  PORT (
 	address: in std_logic_vector(4 downto 0);
 	enable: in std_logic;
 	reset: in std_logic;
 	w_r: in std_logic;
 	clk: in std_logic;
 	data_input: in std_logic_vector(7 downto 0);
 	data_output: out std_logic_vector(7 downto 0)
    );
END memory_ram;

ARCHITECTURE TypeArchitecture OF memory_ram IS
type memory_32_8 is array (0 to 31) of std_logic_vector(7 downto 0);
signal memory_signal: memory_32_8:=(others=> x"00");
signal adress_aux: std_logic_vector(4 downto 0):="00000";
BEGIN
	process(clk, address, w_r, data_input)
	begin
		if clk'event and clk='1' then
			if reset='1' then
				memory_signal<=(others=> x"00");
			elsif enable='1' then
				if w_r='1' then
					memory_signal(to_integer(unsigned(address)))<=data_input;      -- ia elementul dim memorie de la adresa data
					adress_aux<=address;
				else adress_aux<=address;
				end if;
			end if;
		end if;
	end process;

	data_output<=memory_signal(to_integer(unsigned(adress_aux)));

END TypeArchitecture;

// VHDL entity revese_direct_counter, as the project stores it:
--------------------------------------------------------------------------------
-- Project : Memorii FIFO
-- Autor   : Cret Maria-Magdalena 
--------------------------------------------------------------------------------
-- Description : Implementarea unui numarator direct reversibil pe care il vom utiliza in implementarea memoriei FIFO
--------------------------------------------------------------------------------


LIBRARY ieee;
USE ieee.std_logic_1164.all;
USE IEEE.std_logic_unsigned.all;

ENTITY revese_direct_counter IS
  PORT (
 	enable: in std_logic;
 	direction: in std_logic;
 	reset: in std_logic;
 	clk: in std_logic;
 	count: out std_logic_vector(4 downto 0)
    );
END revese_direct_counter;


ARCHITECTURE TypeArchitecture OF revese_direct_counter IS
signal count_aux: std_logic_vector(4 downto 0):= (others=> '0');
BEGIN
	process(clk, direction, enable, reset)
	begin
		if clk'event and clk='1' then
			if reset='1' then
				count_aux<="00000";
			elsif enable='1' then
				if direction='1' then
					count_aux<= count_aux+"00001";
				else 
					count_aux<= count_aux-"00001";
				end if;
			end if;
		end if;
	count<=count_aux;
	end process;

END TypeArchitecture;

// VHDL entity multiplexor_2_1_5_bits, as the project stores it:
--------------------------------------------------------------------------------
-- Project : Mmeorii FIFO
-- Autor   : Cret Maria-Magdalena
--------------------------------------------------------------------------------
-- Description : Implementarea unui multiplexor cu 2 intrari si o iesire pe o cale de 5 biti
--------------------------------------------------------------------------------

LIBRARY ieee;
USE ieee.std_logic_1164.all;

ENTITY multiplexor_2_1_5_bits IS
  PORT (
	a: in std_logic_vector(4 downto 0);
	b: in std_logic_vector(4 downto 0);
	sel: in std_logic;
	result: out std_logic_vector(4 downto 0)
    );
END multiplexor_2_1_5_bits;

ARCHITECTURE TypeArchitecture OF multiplexor_2_1_5_bits IS

BEGIN
	process(a, b, sel)
	begin
		if sel='0' then
			result<=a;
		else
			result<=b;
		end if;
	end process;

END TypeArchitecture;

// VHDL entity unit_command, as the project stores it:
--------------------------------------------------------------------------------
-- Project : Memorii FIFO
-- Autor   : Cret Maria-Magdalena
--------------------------------------------------------------------------------
-- Description : Implementarea unitatii de comanda a intregii memorii
--------------------------------------------------------------------------------

LIBRARY ieee;
USE ieee.std_logic_1164.all;

ENTITY unit_command IS
  PORT (
  push: in std_logic;
  pop: in std_logic;
  clk: in std_logic;
  empty: in std_logic;
  empty_operation: in std_logic;
  full: in std_logic;
  
  reset_empty_operation:out std_logic;
  enable_push: out std_logic;
  enable_pop: out std_logic;
  enable_count: out std_logic;
  direction_count: out std_logic;
  write: out std_logic;
  selection:out std_logic;
  enable_ram: out std_logic
    );
END unit_command;

ARCHITECTURE TypeArchitecture OF unit_command IS
type state_fifo is (Wait_state, Empty_operation_state, Push_state, Pop_state);
signal state, next_state: state_fifo:=Wait_state;
BEGIN

     --- Procesul care trece de la o stare la alta
	process(clk)
	begin
		if clk'event and clk = '1' then
			state <= next_state;
		end if;
	end process;

	--- Procesul care decide noua stare pe baza vechii starii si a intrariilor
	process(state, push, pop, empty, full, empty_operation)
	begin
	case state is
		when Wait_state => if empty_operation='1' then next_state<=Empty_operation_state;
					   elsif push='1' then 
						   if full='0' then
						   	next_state<=Push_state;
						   else
						   	next_state<=Wait_state;
						   end if;
					   elsif pop='1' then next_state<=Pop_state;
						   if empty='0' then
						   	next_state<=Pop_state;
						   else
						   	next_state<=Wait_state;
						   end if;
					   else next_state<=Wait_state;
					   end if;
		when Empty_operation_state => next_state<=Wait_state;
		when Push_state => next_state<=Wait_state;
		when Pop_state => next_state<=Wait_state;
	end case;
	end process;

	--- Procesul care activeaza iesirile in functie de stari
	process(state, push, pop, empty, full, empty_operation)
	begin
	
	reset_empty_operation<='0';
  	enable_push<='0';
  	enable_pop<='0';
  	enable_count<='0';
  	direction_count<='0';
  	write<='0';
  	selection<='0';
  	enable_ram<='0';
  	
	case state is
		when Empty_operation_state => reset_empty_operation<='1';
		when Push_state => enable_push<='1'; write<='1'; enable_count<='1'; direction_count<='1';enable_ram<='1';
		when Pop_state => enable_pop<='1'; selection<='1';enable_count<='1';enable_ram<='1';
		when others => selection<='0';
	end case;	
	end process;	

END TypeArchitecture;

// VHDL entity status_component, as the project stores it:
--------------------------------------------------------------------------------
-- Project : Memorii FIFO
-- Autor   : Cret Maria-Magdalena
--------------------------------------------------------------------------------
-- Description : Implementarea componentei status
--------------------------------------------------------------------------------

LIBRARY ieee;
USE ieee.std_logic_1164.all;

ENTITY status_component IS
  PORT (
  	number_elements: in std_logic_vector(4 downto 0);
  	empty: out std_logic;
  	full: out std_logic
    );
END status_component;

ARCHITECTURE TypeArchitecture OF status_component IS

BEGIN
	process(number_elements)
	begin
	empty<='0';
	full<='0';
		if(number_elements="00000") then
			empty<='1';
		elsif(number_elements="11111") then
			full<='1';
		end if;
	end process;

END TypeArchitecture;
